// Logisim project riscv_project.circ as structural Verilog: 7 circuits, main circuit main
module main (
);

  wire ALU_eq, ALU_lt, ALU_ltu, and_1_out, branch_1_out_5, clock_1_out, clock_2_out, clock_3_out,
       clock_4_out, clock_5_out, clock_7_out, Control_branch, Control_ir_write, Control_mem_write,
       Control_pc_src, Control_pc_write, Control_reg_write, D_MEM_p7, or_1_out;
  wire [1:0] Control_a_src, Control_b_src, Control_reg_src;
  wire [2:0] Control_comp_op, IR_func3;
  wire [3:0] Control_alu_op, Control_mem_size;
  wire [4:0] IR_op, IR_rd, IR_rs1, IR_rs2;
  wire [6:0] IR_func7;
  wire [7:0] D_MEM_p8, D_MEM_p9, D_MEM_p10, D_MEM_p11, I_MEM_p1, I_MEM_p2, I_MEM_p3, I_MEM_p4,
       multiplexer_5_out, multiplexer_6_out, multiplexer_7_out, multiplexer_8_out;
  wire [23:0] register_3_q;
  wire [31:0] ALU_res, IMMDecoder_immout, IR_imm, multiplexer_1_out, multiplexer_2_out, multiplexer_3_out,
       multiplexer_4_out, PC_old_q, PC_q, RegDump_a, RegDump_b, register_1_q, register_2_q, register_4_q;
  wire [31:24] register_3_q_2;

  Multiplexer #(.width(32)) multiplexer_1 (
    .in0({register_3_q_2, register_3_q}), .in1(ALU_res), .out(multiplexer_1_out), .sel(Control_pc_src));
  and and_1 (and_1_out, branch_1_out_5, Control_branch);
  Register #(.width(32)) PC (.D(multiplexer_1_out), .en(or_1_out), .clk(clock_1_out), .Q(PC_q));  // open: clr
  Clock clock_1 (.out(clock_1_out));
  or or_1 (or_1_out, and_1_out, Control_pc_write);
  // RAM #(.addrWidth(16), .enables("line"), .line("quad"), .\type ("nonvolatile")) I_MEM: pin names not known; wires that end beside it: I_MEM_p1, I_MEM_p2, I_MEM_p3, I_MEM_p4
  Contro Control (
    .OP(IR_op), .PCBranch(and_1_out), .func3(IR_func3), .func7(IR_func7), .PC_src(Control_pc_src),
    .PC_write(Control_pc_write), .IR_write(Control_ir_write), .reg_src(Control_reg_src),
    .reg_write(Control_reg_write), .A_src(Control_a_src), .B_src(Control_b_src), .ALU_op(Control_alu_op),
    .comp_op(Control_comp_op), .mem_size(Control_mem_size), .mem_write(Control_mem_write),
    .branch(Control_branch));  // open: out_17
  Register #(.width(32)) PC_old (.D(PC_q), .en(Control_ir_write), .clk(clock_2_out), .Q(PC_old_q));  // open: clr
  Clock clock_2 (.out(clock_2_out));
  // Probe on PC_q
  // Probe on register_4_q
  IR_Decoder IR (
    .Ins({I_MEM_p1, I_MEM_p2, I_MEM_p3, I_MEM_p4}), .w(Control_ir_write), .OP(IR_op), .rd(IR_rd),
    .rs1(IR_rs1), .rs2(IR_rs2), .func3(IR_func3), .func7(IR_func7), .imm(IR_imm));
  // Probe on {register_3_q_2, register_3_q}
  Multiplexer #(.select(2), .width(32)) multiplexer_2 (
    .in0({register_3_q_2, register_3_q}), .in1(register_4_q), .in2(PC_q), .out(multiplexer_2_out),
    .sel(Control_reg_src));  // open: in3
  // Probe on Control_reg_src
  // Probe on IR_op
  RegDum RegDump (
    .Data(multiplexer_2_out), .wr(IR_rd), .rs1(IR_rs1), .rs2(IR_rs2), .we(Control_reg_write), .A(RegDump_a),
    .B(RegDump_b));
  Register #(.width(32)) register_1 (.D(RegDump_a), .en(1'b1), .clk(clock_3_out), .Q(register_1_q));  // open: clr
  Clock clock_3 (.out(clock_3_out));
  Register #(.width(32)) register_2 (.D(RegDump_b), .en(1'b1), .clk(clock_4_out), .Q(register_2_q));  // open: clr
  Clock clock_4 (.out(clock_4_out));
  // Probe on IMMDecoder_immout
  IMMDecode IMMDecoder (.OPcode(IR_op), .IMM(IR_imm), .IMMout(IMMDecoder_immout));
  // Probe on PC_q
  // Probe on PC_old_q
  Multiplexer #(.select(2), .width(32)) multiplexer_3 (
    .in0(register_1_q), .in1(PC_old_q), .in2(PC_q), .out(multiplexer_3_out), .sel(Control_a_src));  // open: in3
  Multiplexer #(.select(2), .width(32)) multiplexer_4 (
    .in0(register_2_q), .in1(IMMDecoder_immout), .in2(32'h4), .out(multiplexer_4_out), .sel(Control_b_src));  // open: in3
  // Probe on Control_a_src
  // Probe on Control_b_src
  ALUU ALU (
    .OP_A(multiplexer_3_out), .OP_B(multiplexer_4_out), .ALUop(Control_alu_op), .Res(ALU_res), .lt(ALU_lt),
    .eq(ALU_eq), .ltu(ALU_ltu));
  Register #(.width(32)) register_3 (
    .D(ALU_res), .en(1'b1), .clk(clock_5_out), .Q({register_3_q_2, register_3_q}));  // open: clr
  Clock clock_5 (.out(clock_5_out));
  Branch branch_1 (.lt(ALU_lt), .eq(ALU_eq), .ltu(ALU_ltu), .compOP(Control_comp_op), .out_5(branch_1_out_5));
  // RAM #(.addrWidth(24), .enables("line"), .line("quad"), .misaligned("true")) D_MEM: pin names not known; wires that end beside it: register_3_q, Control_mem_write, Control_mem_size[0], Control_mem_size[1], Control_mem_size[2], Control_mem_size[3], D_MEM_p7, D_MEM_p8, D_MEM_p9, D_MEM_p10, D_MEM_p11
  Clock clock_6 (.out(D_MEM_p7));
  Multiplexer #(.width(8)) multiplexer_5 (
    .in0(D_MEM_p8), .in1({8{1'b0}}), .out(multiplexer_5_out), .sel(Control_mem_size[0]));
  Multiplexer #(.width(8)) multiplexer_6 (
    .in0(D_MEM_p9), .in1({8{1'b0}}), .out(multiplexer_6_out), .sel(Control_mem_size[1]));
  Multiplexer #(.width(8)) multiplexer_7 (
    .in0(D_MEM_p10), .in1({8{1'b0}}), .out(multiplexer_7_out), .sel(Control_mem_size[2]));
  Multiplexer #(.width(8)) multiplexer_8 (
    .in0(D_MEM_p11), .in1({8{1'b0}}), .out(multiplexer_8_out), .sel(Control_mem_size[3]));
  Register #(.width(32)) register_4 (
    .D({multiplexer_8_out, multiplexer_7_out, multiplexer_6_out, multiplexer_5_out}), .en(1'b1),
    .clk(clock_7_out), .Q(register_4_q));  // open: clr
  Clock clock_7 (.out(clock_7_out));

  // Notes on the sheet:
  //   PC
  //   ALU
  //   MEM
  //   REG_A
  //   PC_old
  //   PC
  //   REG_B
  //   IMM
  //   4
endmodule

module RegDum (
  input  [31:0] Data,
  input  [4:0] wr,
  input  [4:0] rs1,
  input  [4:0] rs2,
  input  we,
  output [31:0] A,
  output [31:0] B
);

  wire and_1_out, and_2_out, and_3_out, and_4_out, and_5_out, and_6_out, and_7_out, and_8_out, and_9_out,
       and_10_out, and_11_out, and_12_out, and_13_out, and_14_out, and_15_out, and_16_out, and_17_out,
       and_18_out, and_19_out, and_20_out, and_21_out, and_22_out, and_23_out, and_24_out, and_25_out,
       and_26_out, and_27_out, and_28_out, and_29_out, and_30_out, and_31_out, and_32_out, clock_1_out,
       decoder_1_out0, decoder_1_out1, decoder_1_out2, decoder_1_out3, decoder_1_out4, decoder_1_out5,
       decoder_1_out6, decoder_1_out7, decoder_2_out0, decoder_2_out1, decoder_2_out2;
  wire [31:0] multiplexer_1_out, multiplexer_2_out, multiplexer_3_out, multiplexer_4_out, multiplexer_5_out,
       multiplexer_6_out, multiplexer_7_out, multiplexer_8_out, register_1_q, register_2_q, register_3_q,
       register_4_q, register_5_q, register_6_q, register_7_q, register_8_q, register_9_q, register_10_q,
       register_11_q, register_12_q, register_13_q, register_14_q, register_15_q, register_16_q,
       register_17_q, register_18_q, register_19_q, register_20_q, register_21_q, register_22_q,
       register_23_q, register_24_q, register_25_q, register_26_q, register_27_q, register_28_q,
       register_29_q, register_30_q, register_31_q, register_32_q;

  Clock clock_1 (.out(clock_1_out));
  Decoder #(.select(3)) decoder_1 (
    .out0(decoder_1_out0), .out1(decoder_1_out1), .out2(decoder_1_out2), .out3(decoder_1_out3),
    .out4(decoder_1_out4), .out5(decoder_1_out5), .out6(decoder_1_out6), .out7(decoder_1_out7),
    .sel(wr[2:0]), .en(we));
  Decoder #(.select(2)) decoder_2 (
    .out0(decoder_2_out0), .out1(decoder_2_out1), .out2(decoder_2_out2), .out3(decoder_2_out2),
    .sel(wr[4:3]), .en(we));
  Register #(.width(32)) register_1 (.D(Data), .en(and_1_out), .clk(clock_1_out), .Q(register_1_q));  // open: clr
  and and_1 (and_1_out, decoder_2_out0, decoder_1_out0);
  Register #(.width(32)) register_2 (.D(Data), .en(and_2_out), .clk(clock_1_out), .Q(register_2_q));  // open: clr
  and and_2 (and_2_out, decoder_2_out1, decoder_1_out0);
  Register #(.width(32)) register_3 (.D(Data), .en(and_3_out), .clk(clock_1_out), .Q(register_3_q));  // open: clr
  and and_3 (and_3_out, decoder_2_out2, decoder_1_out0);
  Register #(.width(32)) register_4 (.D(Data), .en(and_4_out), .clk(clock_1_out), .Q(register_4_q));  // open: clr
  and and_4 (and_4_out, decoder_2_out2, decoder_1_out0);
  Register #(.width(32)) register_5 (.D(Data), .en(and_5_out), .clk(clock_1_out), .Q(register_5_q));  // open: clr
  and and_5 (and_5_out, decoder_2_out0, decoder_1_out1);
  Register #(.width(32)) register_6 (.D(Data), .en(and_6_out), .clk(clock_1_out), .Q(register_6_q));  // open: clr
  and and_6 (and_6_out, decoder_2_out1, decoder_1_out1);
  Register #(.width(32)) register_7 (.D(Data), .en(and_7_out), .clk(clock_1_out), .Q(register_7_q));  // open: clr
  and and_7 (and_7_out, decoder_2_out2, decoder_1_out1);
  Register #(.width(32)) register_8 (.D(Data), .en(and_8_out), .clk(clock_1_out), .Q(register_8_q));  // open: clr
  and and_8 (and_8_out, decoder_2_out2, decoder_1_out1);
  Register #(.width(32)) register_9 (.D(Data), .en(and_9_out), .clk(clock_1_out), .Q(register_9_q));  // open: clr
  and and_9 (and_9_out, decoder_2_out0, decoder_1_out2);
  Register #(.width(32)) register_10 (.D(Data), .en(and_10_out), .clk(clock_1_out), .Q(register_10_q));  // open: clr
  and and_10 (and_10_out, decoder_2_out1, decoder_1_out2);
  Register #(.width(32)) register_11 (.D(Data), .en(and_11_out), .clk(clock_1_out), .Q(register_11_q));  // open: clr
  and and_11 (and_11_out, decoder_2_out2, decoder_1_out2);
  Register #(.width(32)) register_12 (.D(Data), .en(and_12_out), .clk(clock_1_out), .Q(register_12_q));  // open: clr
  and and_12 (and_12_out, decoder_2_out2, decoder_1_out2);
  Register #(.width(32)) register_13 (.D(Data), .en(and_13_out), .clk(clock_1_out), .Q(register_13_q));  // open: clr
  and and_13 (and_13_out, decoder_2_out0, decoder_1_out3);
  Register #(.width(32)) register_14 (.D(Data), .en(and_14_out), .clk(clock_1_out), .Q(register_14_q));  // open: clr
  and and_14 (and_14_out, decoder_2_out1, decoder_1_out3);
  Register #(.width(32)) register_15 (.D(Data), .en(and_15_out), .clk(clock_1_out), .Q(register_15_q));  // open: clr
  and and_15 (and_15_out, decoder_2_out2, decoder_1_out3);
  Register #(.width(32)) register_16 (.D(Data), .en(and_16_out), .clk(clock_1_out), .Q(register_16_q));  // open: clr
  and and_16 (and_16_out, decoder_2_out2, decoder_1_out3);
  Register #(.width(32)) register_17 (.D(Data), .en(and_17_out), .clk(clock_1_out), .Q(register_17_q));  // open: clr
  and and_17 (and_17_out, decoder_2_out0, decoder_1_out4);
  Register #(.width(32)) register_18 (.D(Data), .en(and_18_out), .clk(clock_1_out), .Q(register_18_q));  // open: clr
  and and_18 (and_18_out, decoder_2_out1, decoder_1_out4);
  Register #(.width(32)) register_19 (.D(Data), .en(and_19_out), .clk(clock_1_out), .Q(register_19_q));  // open: clr
  and and_19 (and_19_out, decoder_2_out2, decoder_1_out4);
  Register #(.width(32)) register_20 (.D(Data), .en(and_20_out), .clk(clock_1_out), .Q(register_20_q));  // open: clr
  and and_20 (and_20_out, decoder_2_out2, decoder_1_out4);
  and and_21 (and_21_out, decoder_2_out0, decoder_1_out5);
  and and_22 (and_22_out, decoder_2_out1, decoder_1_out5);
  and and_23 (and_23_out, decoder_2_out2, decoder_1_out5);
  and and_24 (and_24_out, decoder_2_out2, decoder_1_out5);
  Register #(.width(32)) register_21 (.D(Data), .en(and_21_out), .clk(clock_1_out), .Q(register_21_q));  // open: clr
  Register #(.width(32)) register_22 (.D(Data), .en(and_22_out), .clk(clock_1_out), .Q(register_22_q));  // open: clr
  Register #(.width(32)) register_23 (.D(Data), .en(and_23_out), .clk(clock_1_out), .Q(register_23_q));  // open: clr
  Register #(.width(32)) register_24 (.D(Data), .en(and_24_out), .clk(clock_1_out), .Q(register_24_q));  // open: clr
  and and_25 (and_25_out, decoder_2_out0, decoder_1_out6);
  and and_26 (and_26_out, decoder_2_out1, decoder_1_out6);
  and and_27 (and_27_out, decoder_2_out2, decoder_1_out6);
  and and_28 (and_28_out, decoder_2_out2, decoder_1_out6);
  Register #(.width(32)) register_25 (.D(Data), .en(and_25_out), .clk(clock_1_out), .Q(register_25_q));  // open: clr
  Register #(.width(32)) register_26 (.D(Data), .en(and_26_out), .clk(clock_1_out), .Q(register_26_q));  // open: clr
  Register #(.width(32)) register_27 (.D(Data), .en(and_27_out), .clk(clock_1_out), .Q(register_27_q));  // open: clr
  Register #(.width(32)) register_28 (.D(Data), .en(and_28_out), .clk(clock_1_out), .Q(register_28_q));  // open: clr
  Register #(.width(32)) register_29 (.D(Data), .en(and_29_out), .clk(clock_1_out), .Q(register_29_q));  // open: clr
  and and_29 (and_29_out, decoder_2_out0, decoder_1_out7);
  Register #(.width(32)) register_30 (.D(Data), .en(and_30_out), .clk(clock_1_out), .Q(register_30_q));  // open: clr
  and and_30 (and_30_out, decoder_2_out1, decoder_1_out7);
  Register #(.width(32)) register_31 (.D(Data), .en(and_31_out), .clk(clock_1_out), .Q(register_31_q));  // open: clr
  and and_31 (and_31_out, decoder_2_out2, decoder_1_out7);
  Register #(.width(32)) register_32 (.D(Data), .en(and_32_out), .clk(clock_1_out), .Q(register_32_q));  // open: clr
  and and_32 (and_32_out, decoder_2_out2, decoder_1_out7);
  Multiplexer #(.select(3), .width(32)) multiplexer_1 (
    .in0(register_1_q), .in1(register_5_q), .in2(register_9_q), .in3(register_13_q), .in4(register_17_q),
    .in5(register_21_q), .in6(register_25_q), .in7(register_29_q), .out(multiplexer_1_out), .sel(rs2[2:0]));
  Multiplexer #(.select(3), .width(32)) multiplexer_2 (
    .in0(register_1_q), .in1(register_5_q), .in2(register_9_q), .in3(register_13_q), .in4(register_17_q),
    .in5(register_21_q), .in6(register_25_q), .in7(register_29_q), .out(multiplexer_2_out), .sel(rs1[2:0]));
  Multiplexer #(.select(3), .width(32)) multiplexer_3 (
    .in0(register_2_q), .in1(register_6_q), .in2(register_10_q), .in3(register_14_q), .in4(register_18_q),
    .in5(register_22_q), .in6(register_26_q), .in7(register_30_q), .out(multiplexer_3_out), .sel(rs2[2:0]));
  Multiplexer #(.select(3), .width(32)) multiplexer_4 (
    .in0(register_2_q), .in1(register_6_q), .in2(register_10_q), .in3(register_14_q), .in4(register_18_q),
    .in5(register_22_q), .in6(register_26_q), .in7(register_30_q), .out(multiplexer_4_out), .sel(rs1[2:0]));
  Multiplexer #(.select(3), .width(32)) multiplexer_5 (
    .in0(register_3_q), .in1(register_7_q), .in2(register_11_q), .in3(register_15_q), .in4(register_19_q),
    .in5(register_23_q), .in6(register_27_q), .in7(register_31_q), .out(multiplexer_5_out), .sel(rs2[2:0]));
  Multiplexer #(.select(3), .width(32)) multiplexer_6 (
    .in0(register_3_q), .in1(register_7_q), .in2(register_11_q), .in3(register_15_q), .in4(register_19_q),
    .in5(register_23_q), .in6(register_27_q), .in7(register_31_q), .out(multiplexer_6_out), .sel(rs1[2:0]));
  Multiplexer #(.select(3), .width(32)) multiplexer_7 (
    .in0(register_4_q), .in1(register_8_q), .in2(register_12_q), .in3(register_16_q), .in4(register_20_q),
    .in5(register_24_q), .in6(register_28_q), .in7(register_32_q), .out(multiplexer_7_out), .sel(rs2[2:0]));
  Multiplexer #(.select(3), .width(32)) multiplexer_8 (
    .in0(register_4_q), .in1(register_8_q), .in2(register_12_q), .in3(register_16_q), .in4(register_20_q),
    .in5(register_24_q), .in6(register_28_q), .in7(register_32_q), .out(multiplexer_8_out), .sel(rs1[2:0]));
  Multiplexer #(.select(2), .width(32)) multiplexer_9 (
    .in0(multiplexer_2_out), .in1(multiplexer_4_out), .in2(multiplexer_6_out), .in3(multiplexer_8_out),
    .out(A), .sel(rs1[4:3]));
  Multiplexer #(.select(2), .width(32)) multiplexer_10 (
    .in0(multiplexer_1_out), .in1(multiplexer_3_out), .in2(multiplexer_5_out), .in3(multiplexer_7_out),
    .out(B), .sel(rs2[4:3]));

  // Notes on the sheet:
  //   rs1[4:3]
  //   rs2[4:3]
endmodule

module ALUU (
  input  [31:0] OP_A,
  input  [31:0] OP_B,
  input  [3:0] ALUop,
  output [31:0] Res,
  output lt,
  output eq,
  output ltu
);

  wire [31:0] adder_1_out, and_1_out, bit_extender_1_out, bit_extender_2_out, multiplexer_1_out,
       multiplexer_2_out, multiplexer_3_out, not_1_out, or_1_out, shifter_1_out, shifter_2_out,
       shifter_3_out, xor_1_out;

  assign not_1_out = ~OP_B;  // NOT_Gate not_1, 32 bits wide
  Adder #(.width(32)) adder_1 (.a(OP_A), .b(multiplexer_1_out), .out(adder_1_out), .cin(ALUop[0]));  // open: cout
  Multiplexer #(.width(32)) multiplexer_1 (.in0(OP_B), .in1(not_1_out), .out(multiplexer_1_out), .sel(ALUop[0]));
  Shifter #(.width(32)) shifter_1 (.in(OP_A), .\dist (OP_B[4:0]), .out(shifter_1_out));
  Comparator #(.width(32)) comparator_1 (.a(OP_A), .b(OP_B), .eq(eq), .lt(lt));  // open: gt
  Comparator #(.mode("unsigned"), .width(32)) comparator_2 (.a(OP_A), .b(OP_B), .lt(ltu));  // open: gt, eq
  assign xor_1_out = OP_A ^ OP_B;  // XOR_Gate xor_1, 32 bits wide
  Shifter #(.shift("lr"), .width(32)) shifter_2 (.in(OP_A), .\dist (OP_B[4:0]), .out(shifter_2_out));
  Shifter #(.shift("ar"), .width(32)) shifter_3 (.in(OP_A), .\dist (OP_B[4:0]), .out(shifter_3_out));
  assign or_1_out = OP_A | OP_B;  // OR_Gate or_1, 32 bits wide
  assign and_1_out = OP_A & OP_B;  // AND_Gate and_1, 32 bits wide
  Multiplexer #(.width(32)) multiplexer_2 (
    .in0(shifter_2_out), .in1(shifter_3_out), .out(multiplexer_2_out), .sel(ALUop[0]));
  Multiplexer #(.width(32)) multiplexer_3 (.in0(or_1_out), .in1(OP_B), .out(multiplexer_3_out), .sel(ALUop[0]));
  assign bit_extender_1_out = {{31{1'b0}}, lt};  // Bit_Extender bit_extender_1
  assign bit_extender_2_out = {{31{1'b0}}, ltu};  // Bit_Extender bit_extender_2
  Multiplexer #(.select(3), .width(32)) multiplexer_4 (
    .in0(adder_1_out), .in1(shifter_1_out), .in2(bit_extender_1_out), .in3(bit_extender_2_out),
    .in4(xor_1_out), .in5(multiplexer_2_out), .in6(multiplexer_3_out), .in7(and_1_out), .out(Res),
    .sel(ALUop[3:1]));
endmodule

module Contro (
  input  [4:0] OP,
  input  PCBranch,
  input  [2:0] func3,
  input  [6:0] func7,
  output PC_src,
  output PC_write,
  output IR_write,
  output [1:0] reg_src,
  output reg_write,
  output [1:0] A_src,
  output [1:0] B_src,
  output [3:0] ALU_op,
  output [2:0] comp_op,
  output [3:0] mem_size,
  output mem_write,
  output branch,
  output [7:0] out_17
);

  wire and_2_out, and_3_out, and_4_out, clock_1_out, counter_1_carry, decoder_1_out1, decoder_1_out2,
       decoder_1_out3, decoder_1_out4, or_1_out, or_2_out, priority_encoder_1_gs, undriven, undriven_2;
  wire [0:0] and_1_out;
  wire [1:0] priority_encoder_2_out, priority_encoder_3_out;
  wire [2:0] counter_1_q;
  wire [3:0] multiplexer_1_out;
  wire [12:0] rom_1_data;

  Counter #(.max('h4), .width(3)) counter_1 (
    .load(PCBranch), .up(undriven), .count(undriven_2), .clk(clock_1_out), .D(3'b000),
    .carry(counter_1_carry), .Q(counter_1_q));  // open: clr
  // NoConnect on undriven
  // NoConnect on undriven_2
  Clock clock_1 (.out(clock_1_out));
  ROM #(.addrWidth(5), .dataWidth(13)) rom_1 (.addr(OP), .data(rom_1_data));
  // NoConnect on counter_1_carry
  Decoder #(.enable("false"), .select(3)) decoder_1 (
    .out0(IR_write), .out1(decoder_1_out1), .out2(decoder_1_out2), .out3(decoder_1_out3),
    .out4(decoder_1_out4), .sel(counter_1_q));  // open: out5, out6, out7
  and and_1 (and_1_out[0], or_1_out, func7[5]);
  or or_1 (or_1_out, rom_1_data[11], and_2_out);
  and and_2 (and_2_out, func3[2], ~func3[1], func3[0]);  // AND_Gate
  Priority_Encoder #(.select(2)) priority_encoder_1 (
    .in0(rom_1_data[0]), .in1(rom_1_data[1]), .in2(rom_1_data[2]), .out(reg_src), .gs(priority_encoder_1_gs));  // open: in3, en_out, en_in
  Priority_Encoder #(.select(2)) priority_encoder_2 (
    .in0(rom_1_data[3]), .in1(rom_1_data[4]), .in2(IR_write), .out(priority_encoder_2_out));  // open: in3, gs, en_out, en_in
  Priority_Encoder #(.select(2)) priority_encoder_3 (
    .in0(rom_1_data[5]), .in1(rom_1_data[6]), .in2(IR_write), .out(priority_encoder_3_out));  // open: in3, gs, en_out, en_in
  and and_3 (and_3_out, decoder_1_out1, rom_1_data[9]);
  and and_4 (and_4_out, rom_1_data[10], decoder_1_out4);
  Multiplexer #(.width(4)) multiplexer_1 (
    .in0({func3, and_1_out[0]}), .in1(4'b1101), .out(multiplexer_1_out), .sel(rom_1_data[12]));
  and and_5 (reg_write, priority_encoder_1_gs, decoder_1_out4);
  Multiplexer #(.width(2)) multiplexer_2 (.in0(priority_encoder_2_out), .in1(2'b01), .out(A_src), .sel(and_3_out));
  Multiplexer #(.width(2)) multiplexer_3 (.in0(priority_encoder_3_out), .in1(2'b01), .out(B_src), .sel(and_3_out));
  or or_2 (or_2_out, IR_write, and_3_out, rom_1_data[7]);
  Multiplexer #(.width(4)) multiplexer_4 (.in0(multiplexer_1_out), .in1(4'b0000), .out(ALU_op), .sel(or_2_out));
  Multiplexer #(.select(2), .width(4)) multiplexer_5 (
    .in0(4'b0001), .in1(4'b0011), .in2(4'b1111), .out(mem_size), .sel(func3[1:0]));  // open: in3
  and and_6 (mem_write, rom_1_data[8], decoder_1_out3);
  and and_7 (branch, rom_1_data[9], decoder_1_out2);
  or or_3 (PC_write, and_4_out, IR_write);

  assign comp_op = func3;
  assign PC_src = IR_write;

  // Notes on the sheet:
  //   contents of rom_1 (hex, n*v repeats v):
  //   ca 0 0 0 49 d1 0 0 1c8 148 0 0 829 1049 10*0 2a8 4cc 0 4d4
  //   LUI
  //   R
  //   J
  //   B
  //   S
  //   OFFSET
  //   4
  //   ALU
  //   MEM
  //   PC
  //   REG_A
  //   PC_old
  //   PC
  //   REG_B
  //   IMM
endmodule

module IR_Decoder (
  input  [31:0] Ins,
  input  w,
  output [4:0] OP,
  output [4:0] rd,
  output [4:0] rs1,
  output [4:0] rs2,
  output [2:0] func3,
  output [6:0] func7,
  output [31:0] imm
);

  wire clock_1_out;

  Clock clock_1 (.out(clock_1_out));
  Register #(.width(32)) register_1 (
    .D(Ins), .en(w), .clk(clock_1_out), .Q({func7, imm[24:15], func3, imm[11:0]}));  // open: clr

  assign {imm[31:25], imm[14:12]} = {func7, func3};
  assign OP = imm[6:2];
  assign rd = imm[11:7];
  assign rs1 = imm[19:15];
  assign rs2 = imm[24:20];
endmodule

module Branch (
  input  lt,
  input  eq,
  input  ltu,
  input  [2:0] compOP,
  output out_5
);

  wire not_1_out, not_2_out, not_3_out;

  not not_1 (not_1_out, eq);
  not not_2 (not_2_out, lt);
  not not_3 (not_3_out, ltu);
  Multiplexer #(.select(3)) multiplexer_1 (
    .in0(eq), .in1(not_1_out), .in4(lt), .in5(not_2_out), .in6(ltu), .in7(not_3_out), .out(out_5),
    .sel(compOP));  // open: in2, in3
endmodule

module IMMDecode (
  input  [4:0] OPcode,
  input  [31:0] IMM,
  output [31:0] IMMout
);

  wire [2:0] rom_1_data;
  wire [31:0] bit_extender_1_out, bit_extender_2_out, bit_extender_3_out, bit_extender_4_out;

  ROM #(.addrWidth(5), .dataWidth(3)) rom_1 (.addr(OPcode), .data(rom_1_data));
  assign bit_extender_1_out = {{20{IMM[31]}}, IMM[31:20]};  // Bit_Extender bit_extender_1
  assign bit_extender_2_out = {{20{IMM[31]}}, {IMM[31:25], IMM[11:7]}};  // Bit_Extender bit_extender_2
  assign bit_extender_3_out = {{19{IMM[31]}}, {IMM[31], IMM[7], IMM[30:25], IMM[11:8], 1'b0}};  // Bit_Extender bit_extender_3
  assign bit_extender_4_out = {{11{IMM[31]}}, {IMM[31], IMM[19:12], IMM[20], IMM[30:21], 1'b0}};  // Bit_Extender bit_extender_4
  Multiplexer #(.select(3), .width(32)) multiplexer_1 (
    .in0(bit_extender_1_out), .in1(bit_extender_2_out), .in2(bit_extender_3_out),
    .in3({IMM[31:12], {12{1'b0}}}), .in4(bit_extender_4_out), .out(IMMout), .sel(rom_1_data));  // open: in5, in6, in7

  // Notes on the sheet:
  //   contents of rom_1 (hex, n*v repeats v):
  //   5*0 3 0 0 0 1 0 0 0 3 10*0 2 0 0 4
endmodule
